# Fritzing sketch station_meteo (saved by Fritzing 0.9.3b)

parts:
  part = ESP32-38PinWide [part_number=ESP32-38PinWide]
  haul = KY-024 Linear Hall Magnetic Sensor Module [package="Breakout board"]
  pression_alti_temp = Adafruit BME280 [part_number="Adafruit #2652"]
  lcd = OLED 128x64 I2C Monochrome Display GND-VDD
  led = WS2812 RGB LED strip
  Qair = Adafruit CCS811 [part_number="Adafruit #3566"]
  buzzer = MH-FMD buzzer
  5Volt = 4 x AAA Battery Mount
  luxmètre = BH1750

nets:
  VCC: part.3.3, pression_alti_temp.VCC, pression_alti_temp.CS, lcd.VDD, Qair.3.3V, buzzer.Pin_1, luxmètre.ADDR
  N1: part.GPIO35, haul.A0
  GND: part.GND, haul.G, pression_alti_temp.GND, pression_alti_temp.SDO/ADR, lcd.GND, led.GND, Qair.GND, Qair.!WAKE, buzzer.Pin_3, 5Volt.-, luxmètre.GND
  VIN: part.VIN, haul.+, led.VCC, 5Volt.+
  N2: part.GPIO4, haul.D0
  N3: part.GPIO5, buzzer.Pin_2
  N4: part.GPIO18, led.DIN
  N5: part.GPIO21, lcd.SDA, Qair.SDA
  N6: part.GPIO22, pression_alti_temp.SCK/SCL, lcd.SCK, Qair.SCL, luxmètre.SCL
  N7: pression_alti_temp.SDI/SDA, luxmètre.SDA

custom parts:
  ESP32-38PinWide: Generic 38-Pin ESP32 with wide format (only access to one side of pins on a breadboard) based on Stephen Lilley's HiLetgo ESP-WROOM-32 ESP32 ESP-32S Development Board.
  KY-024 Linear Hall Magnetic Sensor Module: KY-024 Linear Hall Magnetic Sensor Module reacts iin the presence of a magnetic field.
  Adafruit BME280: Bosch has stepped up their game with their new BME280 sensor, an environmental sensor with temperature, barometric pressure and humidity! This sensor is great for all sorts of indoor environmental sensing and can even be used in both I2C and SPI! This precision sensor from Bosch is the best low-cost sensing solution for measuring humidity with ±3% accuracy, barometric pressure with ±1 hPa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
  OLED 128x64 I2C Monochrome Display GND-VDD: OLED 128x64 I2C Monochrome Display. Note: there are two variants of this part, this one is the GND VDD SCK SDA variant. The other is VDD GND SCK SDA. Make sure you select the part that matches your module as using the incorrect part will probably destroy your module! In addition the mounting holes are marked on silkscreen but not by default drilled. If you want drilled mounting holes, copy a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
  WS2812 RGB LED strip: WS2812 strip
  Adafruit CCS811: Breathe easy - we finally have an I2C VOC/eCO2 sensor in the Adafruit shop! Add air quality monitoring to your project and with an Adafruit CCS811 Air Quality Sensor Breakout. This sensor from AMS is a gas sensor that can detect a wide range of Volatile Organic Compounds (VOCs) and is intended for indoor air quality monitoring. When connected to your microcontroller (running our library code)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
  MH-FMD buzzer: MH-FMD buzzer.
  BH1750: Light Sensor

// code stored in the sketch: Untitled2.ino
#include <Wire.h>
#include <Adafruit_GFX.h>
#include <Adafruit_SSD1306.h>
#include <Adafruit_NeoPixel.h>
#include <BH1750.h>

// OLED
#define SCREEN_WIDTH 128
#define SCREEN_HEIGHT 64
#define OLED_RESET    -1
Adafruit_SSD1306 display(SCREEN_WIDTH, SCREEN_HEIGHT, &Wire, OLED_RESET);

// NeoPixel
#define LED_PIN    23
#define NUM_LEDS   16
Adafruit_NeoPixel strip(NUM_LEDS, LED_PIN, NEO_GRB + NEO_KHZ800);

// BH1750
BH1750 lightMeter;

// KY-024
#define KY024_DO 34 // Digital Out
#define KY024_AO 35 // Analog Out

// Fan (PWM & Tach)
#define FAN_PWM_PIN  25
#define FAN_TACH_PIN 26

// Variables pour tachymètre
volatile int fanRPM = 0;
volatile int tachCounter = 0;
unsigned long lastTachTime = 0;

// Interruption pour le tachymètre
void IRAM_ATTR tachInterrupt() {
  tachCounter++;
}

void setup() {
  Serial.begin(115200);

  // OLED
  if(!display.begin(SSD1306_SWITCHCAPVCC, 0x3C)) {
    Serial.println(F("Échec OLED"));
    while(true);
  }
  display.clearDisplay();
  display.setTextSize(1);
  display.setTextColor(SSD1306_WHITE);
  display.setCursor(0, 0);
  display.println("Demarrage...");
  display.display();

  // NeoPixel
  strip.begin();
  strip.show(); // Éteint toutes les LEDs

  // BH1750
  Wire.begin();
  lightMeter.begin();

  // KY-024
  pinMode(KY024_DO, INPUT);
  pinMode(KY024_AO, INPUT);

  // Fan PWM
  ledcSetup(0, 25000, 8);  // canal 0, 25kHz, 8 bits
  ledcAttachPin(FAN_PWM_PIN, 0);
  ledcWrite(0, 128); // 50% PWM

  // Fan Tach
  pinMode(FAN_TACH_PIN, INPUT_PULLUP);
  attachInterrupt(digitalPinToInterrupt(FAN_TACH_PIN), tachInterrupt, FALLING);
}

void loop() {
  // KY-024 readings
  int magDigital = digitalRead(KY024_DO);
  int magAnalog = analogRead(KY024_AO);

  // BH1750 luminosité
  float lux = lightMeter.readLightLevel();

  // Calcul RPM fan
  unsigned long currentMillis = millis();
  if (currentMillis - lastTachTime >= 1000) {
    fanRPM = (tachCounter / 2) * 60; // 2 impulsions par tour
    tachCounter = 0;
    lastTachTime = currentMillis;
  }

  // NeoPixel effet simple
  for(int i=0; i<NUM_LEDS; i++) {
    strip.setPixelColor(i, strip.Color(0, 0, 255)); // Bleu
  }
  strip.show();

  // OLED Affichage
  display.clearDisplay();
  display.setCursor(0, 0);
  display.printf("Luminosite: %.1f lx\n", lux);
  display.printf("Mag DO: %d\n", magDigital);
  display.printf("Mag AO: %d\n", magAnalog);
  display.printf("Fan RPM: %d\n", fanRPM);
  display.display();

  delay(500);
}
